# Fritzing sketch Untitled Sketch (saved by Fritzing 0.9.8b)
breadboards: 1

parts:
  Componente1 = Arduino Uno (Rev3)
  Componente2 = SRF05 Ultrasonic Rangefinder
  R1 = Resistor [tolerance=±5% power=0.25 resistance=220 package=THT]
  R2 = Resistor [tolerance=±5% power=0.25 resistance=220 package=THT]
  LED1 = LED - 5mm [color="Red (633nm)" current=0.030 package="5 mm [THT]"]
  AM1 = Multimeter (DC Current)
  P1 = Multimeter straight red probe  # not connected
  P2 = Multimeter straight red probe  # not connected
  J1 = Basic Servo  # not connected

nets:
  N1: Componente1.D2, R1.Pin_0
  N2: Componente1.D3_PWM, R2.Pin_0
  GND: Componente1.GND, Componente2.GND, LED1.anode, AM1.COM_Probe
  N3: R1.Pin_1, LED1.cathode
